# Fritzing sketch lab2 (saved by Fritzing 0.9.4)
breadboards: 1

parts:
  Part1 = Adafruit T-Cobbler Plus [part_number="Adafruit #1989 and #2028"]
  R1 = Resistor [tolerance=±5% resistance=10k package=THT]
  R2 = Resistor [tolerance=±5% resistance=10k package=THT]
  ADC1 = MCP3008 [package=dil16]
  R3 = PHOTOCELL [package=photocell-kit]
  T1 = LM35 Temperature Sensor [package="TO92 [THT]"]
  R4 = Resistor [tolerance=±5% resistance=20k package=THT]

nets:
  +3.3V: Part1.+3.3V, ADC1.VREF, ADC1.VDD, R3.P$1
  N1: Part1.GND, R1.Pin_0, ADC1.DGND, ADC1.AGND
  N2: Part1.MOSI, ADC1.Din
  N3: Part1.MISO, ADC1.Dout
  N4: Part1.SCLK, ADC1.CLK
  N5: Part1.+5V, T1.+Vs
  N6: Part1.CE0, ADC1.CS/SHDN
  N7: R1.Pin_1, ADC1.CH0, R3.P$2
  N8: R2.Pin_0, T1.Vout
  N9: R2.Pin_1, ADC1.CH1, R4.Pin_1
  N10: T1.GND, R4.Pin_0

custom parts:
  Adafruit T-Cobbler Plus: The Raspberry Pi has landed on the Maker World like a 40-GPIO pinned, quad-USB ported, credit card sized bomb of DIY joy. And while you can use most of our great Model B accessories by hooking up our downgrade cable, its probably a good time to upgrade your set up and accessorize using all of the 40 pins. That's why we now carry the Assembled Adafruit Pi T-Cobbler Plus - Breakout + Cable for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
